# Fritzing sketch kitchen-lighting (saved by Fritzing 0.9.3b)
circuit board: 8.5cm x 7cm
breadboards: 1

parts:
  Part1 = Arduino Nano (Rev3.0)
  LED = LED - 5mm [color="Red (633nm)" package="5 mm [THT]"]
  J1 = Power Jack [package=power_jack_slot]
  LedControl = screw terminal, 3 pins
  R = Resistor [tolerance=±5% resistance=220 package=THT]
  5VOUT#2 = screw terminal, 2 pins
  5VIN = Screw terminal - 2 pins [package=THT]
  5VOUT#1 = Screw terminal - 2 pins [package=THT]
  PIRSensor = screw terminal, 3 pins
  12IN = Screw terminal - 2 pins [package=THT]
  5VOUT#3 = Screw terminal - 2 pins [package=THT]
  I2C#2 = Screw terminal - 2 pins [package=THT]
  I2C#1 = Screw terminal - 2 pins [package=THT]
  PotMeter = screw terminal, 3 pins

nets:
  N1: Part1.GND, LED.cathode, LedControl.pin2, 5VOUT#2.pin1, 5VIN.pin1, 5VOUT#1.pin1, PIRSensor.pin2, 5VOUT#3.pin1, PotMeter.pin2
  N2: Part1.D2, PIRSensor.pin1
  N3: Part1.D9, LedControl.pin1, R.Pin_0
  N4: Part1.5V, LedControl.pin3, 5VOUT#2.pin2, 5VIN.pin2, 5VOUT#1.pin2, PIRSensor.pin3, 5VOUT#3.pin2, PotMeter.pin3
  N5: Part1.A5, I2C#2.pin1, I2C#1.pin1
  N6: Part1.A4, I2C#2.pin2, I2C#1.pin2
  N7: Part1.A1, PotMeter.pin1
  N8: LED.anode, R.Pin_1
  N9: J1.GNDBREAK, 12IN.pin1
  N10: J1.PWR, 12IN.pin2

notes:
  gr3go
  I2C
  PWR
  POT
  LED
  5V-IN
  12V
  rev1
  PIR
